// Logisim project MIPS_single_cycle.circ as structural Verilog: 9 circuits, main circuit Main
// ALU
module Main (
);

  wire ALU_alu32_zero, and_1_out, clk, Control_alusrc, Control_branch, Control_jump, Control_memread,
       Control_memtoreg, Control_memwrite, Control_regdst, Control_regwrite;
  wire [1:0] Control_aluop;
  wire [3:0] ALU_control_aluc_out;
  wire [4:0] Instr_memory_im_instruction_2, Instr_memory_im_instruction_3, multiplexer_1_out;
  wire [5:0] Instr_memory_im_instruction_4;
  wire [15:0] Instr_memory_im_instruction;
  wire [27:0] adder_1_out, bit_extender_1_out;
  wire [31:0] a0, a1, a2, a3, adder_2_out, ALU_alu32_result, at, bit_extender_2_out,
       Data_memory_datamem_read_data, fp, gp, k0, k1, multiplexer_2_out, multiplexer_3_out,
       multiplexer_4_out, multiplexer_5_out, PC, ra, Reg_file_regfile_out_read_reg1,
       Reg_file_regfile_out_read_reg2, s0, s1, s2, s3, s4, s5, s6, s7, shifter_1_out, shifter_2_out, sp, t0,
       t1, t2, t3, t4, t5, t6, t7, t8, t9, v0, v1, zero;

  // Probe on zero
  // Probe on at
  // Probe on v0
  // Probe on v1
  // Probe on a0
  // Probe on a1
  // Probe on a2
  // Probe on a3
  // Probe on t0
  // Probe on t1
  // Probe on t2
  // Probe on t3
  // Probe on t4
  // Probe on t5
  // Probe on t6
  // Probe on t7
  // Probe on s0
  // Probe on s1
  // Probe on s2
  // Probe on s3
  // Probe on s4
  // Probe on s5
  // Probe on s6
  // Probe on s7
  // Probe on t8
  // Probe on t9
  // Probe on k0
  // Probe on k1
  // Probe on gp
  // Probe on sp
  // Probe on fp
  // Probe on ra
  Clock clock_1 (.out(clk));
  Register #(.width(32)) u_PC (.D(multiplexer_3_out), .en(1'b1), .clk(clk), .Q(PC));  // open: clr
  // Probe on PC
  Adder #(.width(32)) adder_1 (.a(32'h1), .b(PC), .out({shifter_1_out[31:28], adder_1_out}), .cin(1'b0));  // open: cout
  Instruction_memory Instr_memory (
    .IM_Read_addr(PC),
    .IM_instruction({Instr_memory_im_instruction_4, Instr_memory_im_instruction_3, Instr_memory_im_instruction_2, Instr_memory_im_instruction}));
  assign bit_extender_1_out = {{2{Instr_memory_im_instruction_3[4]}}, {Instr_memory_im_instruction_3, Instr_memory_im_instruction_2, Instr_memory_im_instruction}};  // Bit_Extender bit_extender_1
  Control_unit Control (
    .Instruction_26_32(Instr_memory_im_instruction_4), .RegDst(Control_regdst), .Branch(Control_branch),
    .MemRead(Control_memread), .MemtoReg(Control_memtoreg), .ALUop(Control_aluop),
    .MemWrite(Control_memwrite), .ALUSrc(Control_alusrc), .RegWrite(Control_regwrite), .Jump(Control_jump));
  Shifter #(.width(28)) shifter_1 (.in(bit_extender_1_out), .\dist (5'b00010), .out(shifter_1_out[27:0]));
  Multiplexer #(.width(5)) multiplexer_1 (
    .in0(Instr_memory_im_instruction_2), .in1(Instr_memory_im_instruction[15:11]), .out(multiplexer_1_out),
    .sel(Control_regdst));
  assign bit_extender_2_out = {{16{Instr_memory_im_instruction[15]}}, Instr_memory_im_instruction};  // Bit_Extender bit_extender_2
  Shifter #(.width(32)) shifter_2 (.in(bit_extender_2_out), .\dist (5'b00010), .out(shifter_2_out));
  Adder #(.width(32)) adder_2 (
    .a({shifter_1_out[31:28], adder_1_out}), .b(shifter_2_out), .out(adder_2_out));  // open: cin, cout
  Register_file Reg_file (
    .a3(a3), .a2(a2), .a1(a1), .a0(a0), .v1(v1), .v0(v0), .at(at), .zero(zero),
    .regfile_Read_reg1(Instr_memory_im_instruction_3), .regfile_read_reg2(Instr_memory_im_instruction_2),
    .regfile_write_reg(multiplexer_1_out), .s0(s0), .regfile_data(multiplexer_5_out), .s1(s1), .s2(s2),
    .s3(s3), .s4(s4), .regfile_write(Control_regwrite), .s5(s5), .s6(s6), .s7(s7), .regfile_clk(clk),
    .t0(t0), .t1(t1), .t2(t2), .t3(t3), .t4(t4), .t5(t5), .t6(t6), .t7(t7),
    .regfile_out_read_reg1(Reg_file_regfile_out_read_reg1),
    .regfile_out_read_reg2(Reg_file_regfile_out_read_reg2), .ra(ra), .fp(fp), .sp(sp), .gp(gp), .k1(k1),
    .k0(k0), .t9(t9), .t8(t8));
  Multiplexer #(.width(32)) multiplexer_2 (
    .in0({shifter_1_out[31:28], adder_1_out}), .in1(adder_2_out), .out(multiplexer_2_out), .sel(and_1_out));
  and and_1 (and_1_out, Control_branch, ALU_alu32_zero);
  Multiplexer #(.width(32)) multiplexer_3 (
    .in0(multiplexer_2_out), .in1(shifter_1_out), .out(multiplexer_3_out), .sel(Control_jump));
  ALU_ctrl ALU_control (
    .ALUC_ALUop(Control_aluop), .ALUC_funct(Instr_memory_im_instruction[5:0]), .ALUC_out(ALU_control_aluc_out));
  ALU_32 ALU (
    .ALU32_Cin(1'b0), .ALU32_Ainvert(1'b0), .ALU32_ALUctrl(ALU_control_aluc_out),
    .ALU32_A(Reg_file_regfile_out_read_reg1), .ALU32_B(multiplexer_4_out), .ALU32_Zero(ALU_alu32_zero),
    .ALU32_Result(ALU_alu32_result));  // open: ALU32_Binvert, ALU32_Cout
  Multiplexer #(.width(32)) multiplexer_4 (
    .in0(Reg_file_regfile_out_read_reg2), .in1(bit_extender_2_out), .out(multiplexer_4_out),
    .sel(Control_alusrc));
  Data_memory Data_memory (
    .Datamem_Address(ALU_alu32_result), .Datamem_Write_data(Reg_file_regfile_out_read_reg2),
    .Datamem_Mem_write(Control_memwrite), .Datamem_clk(clk), .Datamem_Mem_read(Control_memread),
    .Datamem_Read_data(Data_memory_datamem_read_data));
  Multiplexer #(.disabled("Z"), .width(32)) multiplexer_5 (
    .in0(ALU_alu32_result), .in1(Data_memory_datamem_read_data), .out(multiplexer_5_out),
    .sel(Control_memtoreg));

  // Notes on the sheet:
  //   Registers
  //   PC gets incremented by 1 word evey clock
endmodule

module ALU_1 (
  input  Ainvert,
  input  Cin,
  input  a,
  input  b,
  input  [1:0] Ctrl,
  input  Binvert,
  input  Less,
  output Co,
  output Set,
  output S,
  output g,
  output p
);

  wire and_1_out, multiplexer_1_out, multiplexer_2_out, not_1_out, not_2_out, or_1_out;

  not not_1 (not_1_out, a);
  not not_2 (not_2_out, b);
  Multiplexer #(.enable("true")) multiplexer_1 (
    .in0(a), .in1(not_1_out), .out(multiplexer_1_out), .sel(Ainvert), .en(1'b1));
  Multiplexer #(.enable("true")) multiplexer_2 (
    .in0(b), .in1(not_2_out), .out(multiplexer_2_out), .sel(Binvert), .en(1'b1));
  Adder #(.width(1)) adder_1 (.a(multiplexer_1_out), .b(multiplexer_2_out), .out(Set), .cin(Cin), .cout(Co));
  and and_1 (and_1_out, multiplexer_1_out, multiplexer_2_out);
  or or_1 (or_1_out, multiplexer_1_out, multiplexer_2_out);
  and and_2 (g, multiplexer_1_out, multiplexer_2_out);
  or or_2 (p, multiplexer_1_out, multiplexer_2_out);
  Multiplexer #(.enable("true"), .select(2)) multiplexer_3 (
    .in0(Set), .in1(and_1_out), .in2(or_1_out), .in3(Less), .out(S), .sel(Ctrl), .en(1'b1));
endmodule

module ALU_4 (
  input  ALU4_Cin,
  input  ALU4_Ainvert,
  input  ALU4_Binvert,
  input  [1:0] ALU4_Ctrl,
  input  [3:0] ALU4_A,
  input  [3:0] ALU4_B,
  input  [3:0] ALU4_Less,
  output [3:0] ALU4_Sum,
  output ALU4_eq,
  output ALU4_setout,
  output ALU4_Cout
);

  wire alu_1_1_g, alu_1_1_p, alu_1_2_g, alu_1_2_p, alu_1_3_g, alu_1_3_p, alu_1_4_g, alu_1_4_p, and_1_out,
       and_2_out, and_3_out, and_4_out, and_5_out, and_6_out, and_7_out, and_8_out, and_9_out, and_10_out,
       or_1_out, or_2_out, or_3_out;

  ALU_1 alu_1_1 (
    .Ainvert(ALU4_Ainvert), .Cin(ALU4_Cin), .a(ALU4_A[0]), .b(ALU4_B[0]), .Ctrl(ALU4_Ctrl),
    .Binvert(ALU4_Binvert), .Less(ALU4_Less[0]), .S(ALU4_Sum[0]), .g(alu_1_1_g), .p(alu_1_1_p));  // open: Co, Set
  ALU_1 alu_1_2 (
    .Ainvert(ALU4_Ainvert), .Cin(or_1_out), .a(ALU4_A[1]), .b(ALU4_B[1]), .Ctrl(ALU4_Ctrl),
    .Binvert(ALU4_Binvert), .Less(ALU4_Less[1]), .S(ALU4_Sum[1]), .g(alu_1_2_g), .p(alu_1_2_p));  // open: Co, Set
  ALU_1 alu_1_3 (
    .Ainvert(ALU4_Ainvert), .Cin(or_2_out), .a(ALU4_A[2]), .b(ALU4_B[2]), .Ctrl(ALU4_Ctrl),
    .Binvert(ALU4_Binvert), .Less(ALU4_Less[2]), .S(ALU4_Sum[2]), .g(alu_1_3_g), .p(alu_1_3_p));  // open: Co, Set
  ALU_1 alu_1_4 (
    .Ainvert(ALU4_Ainvert), .Cin(or_3_out), .a(ALU4_A[3]), .b(ALU4_B[3]), .Ctrl(ALU4_Ctrl),
    .Binvert(ALU4_Binvert), .Less(ALU4_Less[3]), .Set(ALU4_setout), .S(ALU4_Sum[3]), .g(alu_1_4_g),
    .p(alu_1_4_p));  // open: Co
  and and_1 (and_1_out, alu_1_1_p, ALU4_Cin);
  or or_1 (or_1_out, alu_1_1_g, and_1_out);
  and and_2 (and_2_out, alu_1_2_p, alu_1_1_g);
  and and_3 (and_3_out, alu_1_3_g, alu_1_4_p);
  and and_4 (and_4_out, alu_1_2_p, alu_1_1_p, ALU4_Cin);
  and and_5 (and_5_out, alu_1_3_p, alu_1_2_g);
  and and_6 (and_6_out, alu_1_3_p, alu_1_2_p, alu_1_1_g);
  and and_7 (and_7_out, ALU4_Cin, alu_1_2_p, alu_1_1_p, alu_1_3_p);
  and and_8 (and_8_out, alu_1_4_p, alu_1_3_p, alu_1_2_g);
  and and_9 (and_9_out, alu_1_4_p, alu_1_3_p, alu_1_2_p, alu_1_1_g);
  or or_2 (or_2_out, alu_1_2_g, and_2_out, and_4_out);
  or or_3 (or_3_out, and_5_out, and_6_out, alu_1_3_g, and_7_out);
  and and_10 (and_10_out, alu_1_4_p, alu_1_3_p, alu_1_2_p, alu_1_1_p, ALU4_Cin);
  or or_4 (ALU4_Cout, alu_1_4_g, and_3_out, and_8_out, and_9_out, and_10_out);
  nor nor_1 (ALU4_eq, ALU4_Sum[0], ALU4_Sum[1], ALU4_Sum[2], ALU4_Sum[3]);
endmodule

module ALU_32 (
  input  ALU32_Cin,
  input  ALU32_Ainvert,
  input  ALU32_Binvert,
  input  [3:0] ALU32_ALUctrl,
  input  [31:0] ALU32_A,
  input  [31:0] ALU32_B,
  output ALU32_Zero,
  output [31:0] ALU32_Result,
  output ALU32_Cout
);

  wire alu_4_1_alu4_cout, alu_4_1_alu4_eq, alu_4_2_alu4_cout, alu_4_2_alu4_eq, alu_4_3_alu4_cout,
       alu_4_3_alu4_eq, alu_4_4_alu4_cout, alu_4_4_alu4_eq, alu_4_5_alu4_cout, alu_4_5_alu4_eq,
       alu_4_6_alu4_cout, alu_4_6_alu4_eq, alu_4_7_alu4_cout, alu_4_7_alu4_eq, alu_4_8_alu4_eq,
       alu_4_8_alu4_setout, and_1_out, and_2_out, nor_1_out, nor_2_out, nor_3_out, not_1_out, not_2_out,
       not_3_out, or_1_out, or_2_out;
  wire [1:0] or_4_out;
  wire [3:0] bit_extender_1_out;

  or or_1 (or_1_out, ALU32_ALUctrl[1], ALU32_ALUctrl[3]);
  not not_1 (not_1_out, ALU32_ALUctrl[0]);
  not not_2 (not_2_out, ALU32_ALUctrl[3]);
  nor nor_1 (nor_1_out, ALU32_ALUctrl[0], 1'b0);
  not not_3 (not_3_out, ALU32_ALUctrl[3]);
  and and_1 (and_1_out, not_1_out, not_2_out, ALU32_ALUctrl[1], ALU32_ALUctrl[2]);
  nor nor_2 (nor_2_out, nor_1_out, or_1_out);
  nor nor_3 (nor_3_out, ALU32_ALUctrl[0], or_1_out);
  and and_2 (and_2_out, ALU32_ALUctrl[1], ALU32_ALUctrl[2], ALU32_ALUctrl[0], not_3_out);
  or or_2 (or_2_out, and_1_out, and_2_out);
  or or_3 (or_4_out[1], nor_2_out, and_2_out);
  or or_4 (or_4_out[0], and_2_out, nor_3_out);
  ALU_4 alu_4_1 (
    .ALU4_Cin(or_2_out), .ALU4_Ainvert(ALU32_Ainvert), .ALU4_Binvert(or_2_out), .ALU4_Ctrl(or_4_out),
    .ALU4_A(ALU32_A[3:0]), .ALU4_B(ALU32_B[3:0]), .ALU4_Less(bit_extender_1_out),
    .ALU4_Sum(ALU32_Result[3:0]), .ALU4_eq(alu_4_1_alu4_eq), .ALU4_Cout(alu_4_1_alu4_cout));  // open: ALU4_setout
  ALU_4 alu_4_2 (
    .ALU4_Cin(alu_4_1_alu4_cout), .ALU4_Ainvert(ALU32_Ainvert), .ALU4_Binvert(or_2_out),
    .ALU4_Ctrl(or_4_out), .ALU4_A(ALU32_A[7:4]), .ALU4_B(ALU32_B[7:4]), .ALU4_Less(4'b0000),
    .ALU4_Sum(ALU32_Result[7:4]), .ALU4_eq(alu_4_2_alu4_eq), .ALU4_Cout(alu_4_2_alu4_cout));  // open: ALU4_setout
  ALU_4 alu_4_3 (
    .ALU4_Cin(alu_4_2_alu4_cout), .ALU4_Ainvert(ALU32_Ainvert), .ALU4_Binvert(or_2_out),
    .ALU4_Ctrl(or_4_out), .ALU4_A(ALU32_A[11:8]), .ALU4_B(ALU32_B[11:8]), .ALU4_Less(4'b0000),
    .ALU4_Sum(ALU32_Result[11:8]), .ALU4_eq(alu_4_3_alu4_eq), .ALU4_Cout(alu_4_3_alu4_cout));  // open: ALU4_setout
  ALU_4 alu_4_4 (
    .ALU4_Cin(alu_4_3_alu4_cout), .ALU4_Ainvert(ALU32_Ainvert), .ALU4_Binvert(or_2_out),
    .ALU4_Ctrl(or_4_out), .ALU4_A(ALU32_A[15:12]), .ALU4_B(ALU32_B[15:12]), .ALU4_Less(4'b0000),
    .ALU4_Sum(ALU32_Result[15:12]), .ALU4_eq(alu_4_4_alu4_eq), .ALU4_Cout(alu_4_4_alu4_cout));  // open: ALU4_setout
  ALU_4 alu_4_5 (
    .ALU4_Cin(alu_4_4_alu4_cout), .ALU4_Ainvert(ALU32_Ainvert), .ALU4_Binvert(or_2_out),
    .ALU4_Ctrl(or_4_out), .ALU4_A(ALU32_A[19:16]), .ALU4_B(ALU32_B[19:16]), .ALU4_Less(4'b0000),
    .ALU4_Sum(ALU32_Result[19:16]), .ALU4_eq(alu_4_5_alu4_eq), .ALU4_Cout(alu_4_5_alu4_cout));  // open: ALU4_setout
  ALU_4 alu_4_6 (
    .ALU4_Cin(alu_4_5_alu4_cout), .ALU4_Ainvert(ALU32_Ainvert), .ALU4_Binvert(or_2_out),
    .ALU4_Ctrl(or_4_out), .ALU4_A(ALU32_A[23:20]), .ALU4_B(ALU32_B[23:20]), .ALU4_Less(4'b0000),
    .ALU4_Sum(ALU32_Result[23:20]), .ALU4_eq(alu_4_6_alu4_eq), .ALU4_Cout(alu_4_6_alu4_cout));  // open: ALU4_setout
  ALU_4 alu_4_7 (
    .ALU4_Cin(alu_4_6_alu4_cout), .ALU4_Ainvert(ALU32_Ainvert), .ALU4_Binvert(or_2_out),
    .ALU4_Ctrl(or_4_out), .ALU4_A(ALU32_A[27:24]), .ALU4_B(ALU32_B[27:24]), .ALU4_Less(4'b0000),
    .ALU4_Sum(ALU32_Result[27:24]), .ALU4_eq(alu_4_7_alu4_eq), .ALU4_Cout(alu_4_7_alu4_cout));  // open: ALU4_setout
  ALU_4 alu_4_8 (
    .ALU4_Cin(alu_4_7_alu4_cout), .ALU4_Ainvert(ALU32_Ainvert), .ALU4_Binvert(or_2_out),
    .ALU4_Ctrl(or_4_out), .ALU4_A(ALU32_A[31:28]), .ALU4_B(ALU32_B[31:28]), .ALU4_Less(4'b0000),
    .ALU4_Sum(ALU32_Result[31:28]), .ALU4_eq(alu_4_8_alu4_eq), .ALU4_setout(alu_4_8_alu4_setout),
    .ALU4_Cout(ALU32_Cout));
  assign bit_extender_1_out = {{3{1'b0}}, alu_4_8_alu4_setout};  // Bit_Extender bit_extender_1
  and and_3 (ALU32_Zero, alu_4_1_alu4_eq, alu_4_2_alu4_eq, alu_4_3_alu4_eq, alu_4_4_alu4_eq, alu_4_5_alu4_eq, alu_4_6_alu4_eq, alu_4_7_alu4_eq, alu_4_8_alu4_eq);
endmodule

module ALU_ctrl (
  input  [1:0] ALUC_ALUop,
  input  [5:0] ALUC_funct,
  output [3:0] ALUC_out
);

  wire nand_1_out, nand_2_out, not_1_out, or_1_out;

  not not_1 (not_1_out, ALUC_ALUop[1]);
  nand nand_1 (nand_1_out, ALUC_ALUop[0], not_1_out);
  nand nand_2 (nand_2_out, ALUC_funct[1], ALUC_ALUop[1]);
  nand nand_3 (ALUC_out[1], ALUC_funct[2], ALUC_ALUop[1]);
  or or_1 (or_1_out, ALUC_funct[3], ALUC_funct[0]);
  nand nand_4 (ALUC_out[2], nand_2_out, nand_1_out);
  and and_1 (ALUC_out[0], ALUC_ALUop[1], or_1_out);

  assign ALUC_out[3] = 1'b0;
endmodule

module Register_file (
  input  [4:0] regfile_Read_reg1,
  input  [4:0] regfile_read_reg2,
  input  [4:0] regfile_write_reg,
  input  [31:0] regfile_data,
  input  regfile_write,
  input  regfile_clk,
  output [31:0] a3,
  output [31:0] t0,
  output [31:0] a2,
  output [31:0] t1,
  output [31:0] a1,
  output [31:0] t2,
  output [31:0] a0,
  output [31:0] t3,
  output [31:0] v1,
  output [31:0] t4,
  output [31:0] v0,
  output [31:0] t5,
  output [31:0] at,
  output [31:0] t6,
  output [31:0] zero,
  output [31:0] t7,
  output [31:0] regfile_out_read_reg1,
  output [31:0] regfile_out_read_reg2,
  output [31:0] s0,
  output [31:0] ra,
  output [31:0] s1,
  output [31:0] fp,
  output [31:0] s2,
  output [31:0] sp,
  output [31:0] s3,
  output [31:0] gp,
  output [31:0] s4,
  output [31:0] k1,
  output [31:0] s5,
  output [31:0] k0,
  output [31:0] s6,
  output [31:0] t9,
  output [31:0] s7,
  output [31:0] t8
);

  wire and_1_out, and_2_out, and_3_out, and_4_out, and_5_out, and_6_out, and_7_out, and_8_out, and_9_out,
       and_10_out, and_11_out, and_12_out, and_13_out, and_14_out, and_15_out, and_16_out, and_17_out,
       and_18_out, and_19_out, and_20_out, and_21_out, and_22_out, and_23_out, and_24_out, and_25_out,
       and_26_out, and_27_out, and_28_out, and_29_out, and_30_out, and_31_out, and_32_out, decoder_1_out0,
       decoder_1_out1, decoder_1_out2, decoder_1_out3, decoder_1_out4, decoder_1_out5, decoder_1_out6,
       decoder_1_out7, decoder_1_out8, decoder_1_out9, decoder_1_out10, decoder_1_out11, decoder_1_out12,
       decoder_1_out13, decoder_1_out14, decoder_1_out15, decoder_1_out16, decoder_1_out17, decoder_1_out18,
       decoder_1_out19, decoder_1_out20, decoder_1_out21, decoder_1_out22, decoder_1_out23, decoder_1_out24,
       decoder_1_out25, decoder_1_out26, decoder_1_out27, decoder_1_out28, decoder_1_out29, decoder_1_out30,
       decoder_1_out31;

  Decoder #(.enable("false"), .select(5)) decoder_1 (
    .out0(decoder_1_out0), .out1(decoder_1_out1), .out2(decoder_1_out2), .out3(decoder_1_out3),
    .out4(decoder_1_out4), .out5(decoder_1_out5), .out6(decoder_1_out6), .out7(decoder_1_out7),
    .out8(decoder_1_out8), .out9(decoder_1_out9), .out10(decoder_1_out10), .out11(decoder_1_out11),
    .out12(decoder_1_out12), .out13(decoder_1_out13), .out14(decoder_1_out14), .out15(decoder_1_out15),
    .out16(decoder_1_out16), .out17(decoder_1_out17), .out18(decoder_1_out18), .out19(decoder_1_out19),
    .out20(decoder_1_out20), .out21(decoder_1_out21), .out22(decoder_1_out22), .out23(decoder_1_out23),
    .out24(decoder_1_out24), .out25(decoder_1_out25), .out26(decoder_1_out26), .out27(decoder_1_out27),
    .out28(decoder_1_out28), .out29(decoder_1_out29), .out30(decoder_1_out30), .out31(decoder_1_out31),
    .sel(regfile_write_reg));
  and and_1 (and_1_out, decoder_1_out0, regfile_write);
  and and_2 (and_2_out, decoder_1_out1, regfile_write);
  and and_3 (and_3_out, decoder_1_out2, regfile_write);
  and and_4 (and_4_out, decoder_1_out3, regfile_write);
  and and_5 (and_5_out, decoder_1_out4, regfile_write);
  and and_6 (and_6_out, decoder_1_out5, regfile_write);
  and and_7 (and_7_out, decoder_1_out6, regfile_write);
  and and_8 (and_8_out, decoder_1_out7, regfile_write);
  and and_9 (and_9_out, decoder_1_out8, regfile_write);
  and and_10 (and_10_out, decoder_1_out9, regfile_write);
  and and_11 (and_11_out, decoder_1_out10, regfile_write);
  and and_12 (and_12_out, decoder_1_out11, regfile_write);
  and and_13 (and_13_out, decoder_1_out12, regfile_write);
  and and_14 (and_14_out, decoder_1_out13, regfile_write);
  and and_15 (and_15_out, decoder_1_out14, regfile_write);
  and and_16 (and_16_out, decoder_1_out15, regfile_write);
  and and_17 (and_17_out, decoder_1_out16, regfile_write);
  and and_18 (and_18_out, decoder_1_out17, regfile_write);
  and and_19 (and_19_out, decoder_1_out18, regfile_write);
  and and_20 (and_20_out, decoder_1_out19, regfile_write);
  and and_21 (and_21_out, decoder_1_out20, regfile_write);
  and and_22 (and_22_out, decoder_1_out21, regfile_write);
  and and_23 (and_23_out, decoder_1_out22, regfile_write);
  and and_24 (and_24_out, decoder_1_out23, regfile_write);
  and and_25 (and_25_out, decoder_1_out24, regfile_write);
  and and_26 (and_26_out, decoder_1_out25, regfile_write);
  and and_27 (and_27_out, decoder_1_out26, regfile_write);
  and and_28 (and_28_out, decoder_1_out27, regfile_write);
  and and_29 (and_29_out, decoder_1_out28, regfile_write);
  and and_30 (and_30_out, decoder_1_out29, regfile_write);
  and and_31 (and_31_out, decoder_1_out30, regfile_write);
  and and_32 (and_32_out, decoder_1_out31, regfile_write);
  Register #(.width(32)) register_1 (.D(regfile_data), .en(and_1_out), .Q(zero), .clk(regfile_clk), .clr(1'b0));
  Register #(.width(32)) register_2 (.D(regfile_data), .en(and_5_out), .Q(a0), .clk(regfile_clk), .clr(1'b0));
  Register #(.width(32)) register_3 (.D(regfile_data), .en(and_9_out), .Q(t0), .clk(regfile_clk), .clr(1'b0));
  Register #(.width(32)) register_4 (.D(regfile_data), .en(and_13_out), .Q(t4), .clk(regfile_clk), .clr(1'b0));
  Register #(.width(32)) register_5 (.D(regfile_data), .en(and_17_out), .Q(s0), .clk(regfile_clk), .clr(1'b0));
  Register #(.width(32)) register_6 (.D(regfile_data), .en(and_21_out), .Q(s4), .clk(regfile_clk), .clr(1'b0));
  Register #(.width(32)) register_7 (.D(regfile_data), .en(and_25_out), .Q(t8), .clk(regfile_clk), .clr(1'b0));
  Register #(.width(32)) register_8 (.D(regfile_data), .en(and_29_out), .Q(gp), .clk(regfile_clk), .clr(1'b0));
  Register #(.width(32)) register_9 (.D(regfile_data), .en(and_2_out), .Q(at), .clk(regfile_clk), .clr(1'b0));
  Register #(.width(32)) register_10 (.D(regfile_data), .en(and_6_out), .Q(a1), .clk(regfile_clk), .clr(1'b0));
  Register #(.width(32)) register_11 (.D(regfile_data), .en(and_10_out), .Q(t1), .clk(regfile_clk), .clr(1'b0));
  Register #(.width(32)) register_12 (.D(regfile_data), .en(and_14_out), .Q(t5), .clk(regfile_clk), .clr(1'b0));
  Register #(.width(32)) register_13 (.D(regfile_data), .en(and_18_out), .Q(s1), .clk(regfile_clk), .clr(1'b0));
  Register #(.width(32)) register_14 (.D(regfile_data), .en(and_22_out), .Q(s5), .clk(regfile_clk), .clr(1'b0));
  Register #(.width(32)) register_15 (.D(regfile_data), .en(and_26_out), .Q(t9), .clk(regfile_clk), .clr(1'b0));
  Register #(.width(32)) register_16 (.D(regfile_data), .en(and_30_out), .Q(sp), .clk(regfile_clk), .clr(1'b0));
  Register #(.width(32)) register_17 (.D(regfile_data), .en(and_3_out), .Q(v0), .clk(regfile_clk), .clr(1'b0));
  Register #(.width(32)) register_18 (.D(regfile_data), .en(and_7_out), .Q(a2), .clk(regfile_clk), .clr(1'b0));
  Register #(.width(32)) register_19 (.D(regfile_data), .en(and_11_out), .Q(t2), .clk(regfile_clk), .clr(1'b0));
  Register #(.width(32)) register_20 (.D(regfile_data), .en(and_15_out), .Q(t6), .clk(regfile_clk), .clr(1'b0));
  Register #(.width(32)) register_21 (.D(regfile_data), .en(and_19_out), .Q(s2), .clk(regfile_clk), .clr(1'b0));
  Register #(.width(32)) register_22 (.D(regfile_data), .en(and_23_out), .Q(s6), .clk(regfile_clk), .clr(1'b0));
  Register #(.width(32)) register_23 (.D(regfile_data), .en(and_27_out), .Q(k0), .clk(regfile_clk), .clr(1'b0));
  Register #(.width(32)) register_24 (.D(regfile_data), .en(and_31_out), .Q(fp), .clk(regfile_clk), .clr(1'b0));
  Register #(.width(32)) register_25 (.D(regfile_data), .en(and_4_out), .Q(v1), .clk(regfile_clk), .clr(1'b0));
  Register #(.width(32)) register_26 (.D(regfile_data), .en(and_8_out), .Q(a3), .clk(regfile_clk), .clr(1'b0));
  Register #(.width(32)) register_27 (.D(regfile_data), .en(and_12_out), .Q(t3), .clk(regfile_clk), .clr(1'b0));
  Register #(.width(32)) register_28 (.D(regfile_data), .en(and_16_out), .Q(t7), .clk(regfile_clk), .clr(1'b0));
  Register #(.width(32)) register_29 (.D(regfile_data), .en(and_20_out), .Q(s3), .clk(regfile_clk), .clr(1'b0));
  Register #(.width(32)) register_30 (.D(regfile_data), .en(and_24_out), .Q(s7), .clk(regfile_clk), .clr(1'b0));
  Register #(.width(32)) register_31 (.D(regfile_data), .en(and_28_out), .Q(k1), .clk(regfile_clk), .clr(1'b0));
  Register #(.width(32)) register_32 (.D(regfile_data), .en(and_32_out), .Q(ra), .clk(regfile_clk), .clr(1'b0));
  Multiplexer #(.select(5), .width(32)) multiplexer_1 (
    .in0(zero), .in1(at), .in2(v0), .in3(v1), .in4(a0), .in5(a1), .in6(a2), .in7(a3), .in8(t0), .in9(t1),
    .in10(t2), .in11(t3), .in12(t4), .in13(t5), .in14(t6), .in15(t7), .in16(s0), .in17(s1), .in18(s2),
    .in19(s3), .in20(s4), .in21(s5), .in22(s6), .in23(s7), .in24(t8), .in25(t9), .in26(k0), .in27(k1),
    .in28(gp), .in29(sp), .in30(fp), .in31(ra), .out(regfile_out_read_reg2), .sel(regfile_read_reg2));
  Multiplexer #(.select(5), .width(32)) multiplexer_2 (
    .in0(zero), .in1(at), .in2(v0), .in3(v1), .in4(a0), .in5(a1), .in6(a2), .in7(a3), .in8(t0), .in9(t1),
    .in10(t2), .in11(t3), .in12(t4), .in13(t5), .in14(t6), .in15(t7), .in16(s0), .in17(s1), .in18(s2),
    .in19(s3), .in20(s4), .in21(s5), .in22(s6), .in23(s7), .in24(t8), .in25(t9), .in26(k0), .in27(k1),
    .in28(gp), .in29(sp), .in30(fp), .in31(ra), .out(regfile_out_read_reg1), .sel(regfile_Read_reg1));

  // Notes on the sheet:
  //   $zero
  //   $a0
  //   $t0
  //   $t4
  //   $s0
  //   $s4
  //   $t8
  //   $gp
  //   $at
  //   $a1
  //   $t1
  //   $t5
  //   $s1
  //   $s5
  //   $sp
  //   $v0
  //   $a2
  //   $t2
  //   $t6
  //   $s2
  //   $s6
  //   $k0
  //   $fp
  //   $v1
  //   $a3
  //   $t3
  //   $t7
  //   $s3
  //   $s7
  //   $k1
  //   $ra
  //   Reg31
endmodule

module Instruction_memory (
  input  [31:0] IM_Read_addr,
  output [31:0] IM_instruction
);

  ROM #(.addrWidth(24), .dataWidth(32)) rom_1 (.addr(IM_Read_addr[23:0]), .data(IM_instruction));

  // Notes on the sheet:
  //   contents of rom_1 (hex, n*v repeats v):
  //   14b4820 14b4822 14b482a 14b4824 14b4825 8c090000 ac090000 0 8000001
  //   Use external files to upload the machine code
endmodule

module Data_memory (
  input  [31:0] Datamem_Address,
  input  [31:0] Datamem_Write_data,
  input  Datamem_Mem_write,
  input  Datamem_clk,
  input  Datamem_Mem_read,
  output [31:0] Datamem_Read_data
);

  RAM #(.addrWidth(24), .asyncread("true"), .dataWidth(32), .\type ("nonvolatile")) ram_1 (
    .addr(Datamem_Address[23:0]), .we(Datamem_Mem_write), .oe(Datamem_Mem_read), .clk(Datamem_clk),
    .din(Datamem_Write_data), .dout(Datamem_Read_data));

  // Notes on the sheet:
  //   24-bit address lines -> 16 MiB of memory
endmodule

module Control_unit (
  input  [5:0] Instruction_26_32,
  output RegDst,
  output Branch,
  output MemRead,
  output MemtoReg,
  output [1:0] ALUop,
  output MemWrite,
  output ALUSrc,
  output RegWrite,
  output Jump
);

  wire and_1_out, and_2_out, and_3_out, nand_1_out, nand_2_out, nand_3_out, nand_4_out, not_1_out, not_2_out,
       not_3_out, not_4_out, not_5_out, not_6_out, not_7_out, not_8_out, not_9_out, not_10_out, not_11_out,
       not_12_out, or_1_out, or_2_out, or_3_out, or_4_out;

  not not_1 (not_1_out, Instruction_26_32[3]);
  not not_2 (not_2_out, Instruction_26_32[4]);
  or or_1 (or_1_out, Instruction_26_32[4], Instruction_26_32[3], Instruction_26_32[5]);
  not not_3 (not_3_out, Instruction_26_32[2]);
  and and_1 (and_1_out, Instruction_26_32[1], Instruction_26_32[0]);
  or or_2 (or_2_out, Instruction_26_32[1], Instruction_26_32[0], or_1_out);
  and and_2 (and_2_out, not_2_out, not_3_out, Instruction_26_32[5], and_1_out);
  or or_3 (or_3_out, or_2_out, Instruction_26_32[2]);
  or or_4 (or_4_out, or_2_out, not_3_out);
  not not_4 (not_4_out, or_3_out);
  not not_5 (not_5_out, or_4_out);
  nand nand_1 (nand_1_out, Instruction_26_32[3], and_2_out);
  and and_3 (and_3_out, Instruction_26_32[3], and_2_out);
  nand nand_2 (nand_2_out, and_2_out, not_1_out);
  not not_6 (not_6_out, Instruction_26_32[0]);
  not not_7 (not_7_out, Instruction_26_32[3]);
  not not_8 (not_8_out, Instruction_26_32[4]);
  not not_9 (not_9_out, Instruction_26_32[5]);
  not not_10 (not_10_out, nand_2_out);
  nand nand_3 (nand_3_out, or_3_out, nand_2_out);
  not not_11 (not_11_out, Instruction_26_32[2]);
  nand nand_4 (nand_4_out, nand_2_out, nand_1_out);
  and and_4 (Jump, not_6_out, not_11_out, not_7_out, not_8_out, Instruction_26_32[1], not_9_out);
  and and_5 (ALUSrc, nand_4_out, not_12_out);
  and and_6 (RegWrite, nand_3_out, not_12_out);
  not not_12 (not_12_out, Jump);
  and and_7 (RegDst, not_4_out, not_12_out);
  and and_8 (Branch, not_5_out, not_12_out);
  and and_9 (MemRead, not_10_out, not_12_out);
  and and_10 (ALUop[0], not_12_out, not_5_out);
  and and_11 (ALUop[1], not_4_out, not_12_out);
  and and_12 (MemWrite, and_3_out, not_12_out);

  assign MemtoReg = MemRead;
endmodule
